# Fritzing sketch LED SX Wiring (saved by Fritzing 0.9.9b)
circuit board: 8.46667cm x 5.64444cm
breadboards: 1

parts:
  J1 = Raspberry Pi Header 40pin [package=THT]
  LED1 = LED - 5mm [color="Red (633nm)" current=0.030 package="5 mm [THT]"]
  R2 = Resistor [tolerance=±5% power=0.25 resistance=220 package=THT]
  LED2 = LED - 5mm [color="Yellow (595nm)" current=0.030 package="5 mm [THT]"]
  R3 = Resistor [tolerance=±5% power=0.25 resistance=220 package=THT]
  LED3 = LED - 5mm [color="Green (555nm)" current=0.030 package="5 mm [THT]"]
  R4 = Resistor [tolerance=±5% power=0.25 resistance=220 package=THT]
  R5 = Resistor [tolerance=±5% power=0.25 resistance=1k package=THT]
  S1 = Pushbutton [package="[THT]"]
  R6 = Resistor [tolerance=±5% power=0.25 resistance=10k package=THT]

nets:
  N1: J1.3V3, S1.Pin_1, S1.Pin_2
  N2: J1.GND, R2.Pin_0, R3.Pin_0, R4.Pin_0, R6.Pin_0
  N3: J1.IO17, R5.Pin_0
  N4: J1.IO18, LED1.anode
  N5: J1.IO23, LED2.anode
  N6: J1.IO24, LED3.anode
  N7: LED1.cathode, R4.Pin_1
  N8: R2.Pin_1, LED2.cathode
  N9: R3.Pin_1, LED3.cathode
  N10: R5.Pin_1, S1.Pin_3, S1.Pin_4, R6.Pin_1

custom parts:
  Raspberry Pi Header 40pin: Raspberry Pi 40 pin header - for creating your own shields. (Mar 2020, bb: make breadboard friendly (.4in pin spacing) and add labels. Schematic add labels. PCB make oblong pins to allow routing traces between the pins.)
