# Fritzing sketch Pico LCD Clock (saved by Fritzing 0.9.9b)
breadboards: 1

parts:
  Mod1 = Raspberry Pi Pico
  LCM1602_IIC1 = LCM1602 IIC [part_number="LCM1602 IIC" chip_label="LCM1602 IIC" package="DIP (Dual Inline) [THT]"]
  LCD1 = LCD screen
  R1 = Resistor [tolerance=±5% power=0.25 resistance=220 package=THT]
  R2 = Photocell (LDR) [package=THT]

nets:
  N1: Mod1.pin_1, LCM1602_IIC1.SDA
  N2: Mod1.pin_2, LCM1602_IIC1.SCL
  N3: Mod1.pin_3, Mod1.pin_8, Mod1.pin_13, Mod1.pin_18, Mod1.pin_23, Mod1.pin_28, Mod1.pin_33, Mod1.pin_38, Mod1.pin_42, LCM1602_IIC1.GND, R1.Pin_1
  N4: Mod1.pin_20, LCM1602_IIC1.LED_A
  N5: Mod1.pin_34, R1.Pin_0, R2.pin_1
  N6: Mod1.pin_36, R2.pin_0
  N7: Mod1.pin_40, LCM1602_IIC1.VCC
  VSS: LCM1602_IIC1.VSS, LCD1.VSS
  VDD: LCM1602_IIC1.VDD, LCD1.VDD
  N8: LCM1602_IIC1.V0, LCD1.V0
  N9: LCM1602_IIC1.RS, LCD1.RS
  N10: LCM1602_IIC1.RW, LCD1.R/W
  N11: LCM1602_IIC1.E, LCD1.E
  N12: LCM1602_IIC1.D0, LCD1.DB0
  N13: LCM1602_IIC1.D1, LCD1.DB1
  N14: LCM1602_IIC1.D2, LCD1.DB2
  N15: LCM1602_IIC1.D3, LCD1.DB3
  N16: LCM1602_IIC1.D4, LCD1.DB4
  N17: LCM1602_IIC1.D5, LCD1.DB5
  N18: LCM1602_IIC1.D6, LCD1.DB6
  N19: LCM1602_IIC1.D7, LCD1.DB7
  N20: LCM1602_IIC1.A, LCD1.LED+
  N21: LCM1602_IIC1.K, LCD1.LED-

custom parts:
  Raspberry Pi Pico: Raspberry Pi Pico. Based around the RP2040 microcontroller the Pico is a low cost microcontroller device bringing Raspberry Pi quality, cost, and easy of use to the microcontroller space. Jan 2021, Split part in to two versions: tht (this one) and SMD. This one will drill holes for a .1 in header in pcb to allow plugging in the module as well as providing pads to solder the module to the top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
  LCM1602 IIC: I2C-Module to use a 1602 or 2004 LCD on with the wire.h libory Serial LCD Modul
